# Fritzing sketch boxy-brown (saved by Fritzing 0.9.2b)

parts:
  RF2 = nRF8001 Bluetooth LE Breakout
  Part1 = Arduino Uno (Rev3) - ICSP  # not connected
  Part3 = Arduino MP3 Player Shield
  SP1 = SPEAKER [package=pcb_mount_speaker]

nets:
  N1: RF2.SCK, Part3.5V-SCK
  N2: RF2.MISO, Part3.MISO
  N3: RF2.MOSI, Part3.5V-MOSI
  N4: RF2.REQ, Part3.D10
  N5: RF2.RDY, Part3.MP3-DREQ
  N6: RF2.RST, Part3.5V-SD-CS
  GND: RF2.GND, Part3.GND
  VIN: RF2.VIN, Part3.VCC
  N7: Part3.GBUF, SP1.-
  N8: Part3.RIGHT, SP1.+

notes:
  BOXY BROWN
  http://j.mp/boxy-brown
  PART LIST
  ---
  * Arduino Uno V3
  * Bluefruit LE ( nRF8001 )
  * Adafruit Music Maker MP3 Shield
  * 3" Diameter 4 Ohm 3 Watt Speaker
  I could not find a Fritzing part for the Adafruit Music Maker MP3 Shield, but the Sparkfun one OK.

custom parts:
  nRF8001 Bluetooth LE Breakout: nRF8001 Breakout Board
